# Fritzing sketch mk4 (saved by Fritzing 0.9.3b)
breadboards: 1

parts:
  Pico1 = Raspberry Pi Pico
  IC1 = IC, DIP package, 8 pins [chip_label=IC]
  S1 = Tilt Switch [package=THT]
  C1 = Tantalum Capacitor [capacitance=1μF package="100 mil [THT, tantalum]"]
  R1 = Resistor [tolerance=±5% resistance=1k package=THT]
  R2 = Resistor [tolerance=±5% resistance=220 package=THT]

nets:
  N1: Pico1.GND, IC1.pin4, S1.Pin_2, C1.+, R1.Pin_1
  N2: Pico1.GP28_A2, IC1.pin1, R2.Pin_0
  N3: IC1.pin2, R1.Pin_0, R2.Pin_1
  N4: IC1.pin3, S1.Pin_1, C1.-

custom parts:
  Raspberry Pi Pico: Raspberry Pi Pico. Based around the RP2040 microcontroller the Pico is a low cost microcontroller device bringing Raspberry Pi quality, cost, and easy of use to the microcontroller space.
