# Fritzing sketch mk5 (saved by Fritzing 0.9.3b)
breadboards: 1

parts:
  Pico1 = Raspberry Pi Pico
  J1 = female pin header, 6 pins [form="♀ (female)"]
  J2 = Piezo Speaker
  J3 = female pin header, 4 pins [form="♀ (female)"]

nets:
  N1: Pico1.VBUS, J3.pin2
  N2: Pico1.GND, J1.pin2, J2.pin1, J3.pin1
  N3: Pico1.3V3, J1.pin1
  N4: Pico1.GP15, J2.pin2
  N5: Pico1.GP6, J3.pin3
  N6: Pico1.GP1, J1.pin3
  N7: Pico1.GP0, J1.pin4

custom parts:
  Raspberry Pi Pico: Raspberry Pi Pico. Based around the RP2040 microcontroller the Pico is a low cost microcontroller device bringing Raspberry Pi quality, cost, and easy of use to the microcontroller space.
